# Fritzing sketch hardware circuit (saved by Fritzing 0.9.2b)
breadboards: 1

parts:
  元件1 = Arduino Uno (Rev3)
  ADXL345 = Triple Axis Accelerometer Breakout - ADXL345
  Buzzer = Grove Buzz
  Vibration_Motor = Grove Button
  U1 = Battery Holders [package=lipo-1100mAh]

nets:
  N1: 元件1.A4/SDA, ADXL345.SDA
  N2: 元件1.A5/SCL, ADXL345.SCL
  N3: 元件1.D5_PWM, Buzzer.SIG
  N4: 元件1.D6_PWM, Vibration_Motor.SIG
  VCC: 元件1.5V, ADXL345.VCC, ADXL345.CS, Buzzer.VCC, Vibration_Motor.VCC
  GND: 元件1.GND, ADXL345.GND, Buzzer.GND, Vibration_Motor.GND, U1.-
  N5: 元件1.VIN, U1.+
